# Fritzing sketch robotCircuit-JM (saved by Fritzing 0.9.3b)
breadboards: 1

parts:
  Part1 = Adafruit Motor/Stepper/Servo Shield [part_number="Adafruit #1438"]
  J1 = female pin header, 8 pins [form="♀ (female)"]
  Part2 = Arduino Uno (Rev3)  # not connected
  J2 = female pin header, 8 pins [form="♀ (female)"]
  VCC1 = Battery block 9V
  M1 = DC Motor
  M2 = DC Motor
  M3 = DC Motor
  M4 = DC Motor
  KY-1 = Keyes Hall Effect Sensor [package=THT]
  R1 = Resistor [tolerance=±5% resistance=10k package="2010 [SMD]"]

nets:
  N1: Part1.M2A, M1.pin_2, M2.pin_2
  N2: Part1.M2B, M1.pin_1, M2.pin_1
  N3: Part1.M1B, M3.pin_2, M4.pin_2
  N4: Part1.M1A, M3.pin_1, M4.pin_1
  N5: Part1.GND, Part1.N$44, J2.pin1, VCC1.-
  N6: Part1.VMOTOR, VCC1.+
  N7: Part1.+5V, Part1.N$141, J1.pin1
  N8: Part1.D3, KY-1.signal, R1.Pin_1
  N9: Part1.N$36, J2.pin2
  N10: Part1.N$47, J2.pin3
  N11: Part1.N$50, J2.pin4
  N12: Part1.N$57, J2.pin5
  N13: Part1.N$60, J2.pin6
  N14: Part1.N$67, J2.pin7, KY-1.power
  N15: Part1.N$70, J2.pin8
  N16: Part1.N$142, J1.pin2, KY-1.ground, R1.Pin_0
  N17: Part1.N$143, J1.pin3
  N18: Part1.N$144, J1.pin5
  N19: Part1.N$145, J1.pin4
  N20: Part1.N$146, J1.pin6
  N21: Part1.N$147, J1.pin7
  N22: Part1.N$148, J1.pin8

custom parts:
  Adafruit Motor/Stepper/Servo Shield: The original Adafruit Motorshield kit is one of our most beloved kits, which is why we decided to make something even better. We have upgraded the shield kit to make the bestest, easiest way to drive DC and Stepper motors. This shield will make quick work of your next robotics project! We kept the ability to drive up to 4 DC motors or 2 stepper motors, but added many improvements: Instead of a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
  Keyes Hall Effect Sensor: Keyes Magnetic Hall Effect Sensor Module for Arduino. Working voltage: 4.5V-25V.
